# Fritzing sketch diy-spacemouse.fz (saved by Fritzing 1.0.6)
breadboards: 1

parts:
  Part1 = Adafruit TLV493D
  Part2 = Adafruit QT Py RP2040 [part_number="Adafruit #4900"]
  Part3 = LED Sequin - Emerald Green [part_number=1756]
  S1 = Pushbutton [package="[THT]"]
  S2 = Pushbutton [package="[THT]"]
  Part4 = LED Sequin - Emerald Green [part_number=1756]
  Part5 = LED Sequin - Emerald Green [part_number=1756]

nets:
  GND: Part1.GND, Part2.GND, Part3.-, S1.Pin_1, S1.Pin_2, S2.Pin_1, S2.Pin_2, Part4.-, Part5.-
  VCC: Part1.VCC, Part2.+3V3, Part3.+, Part4.+, Part5.+
  N1: Part1.SCL, Part2.SCL1
  N2: Part1.SDA, Part2.SDA1
  N3: Part2.A2, S1.Pin_3, S1.Pin_4
  N4: Part2.SDA, S2.Pin_3, S2.Pin_4

custom parts:
  Adafruit TLV493D: The TLV493D 3-axis magnetometer is a great little sensor for detecting magnets in 3D. The manufacturer Infineon suggests it could be used to make a joystick! You could also use it for other cool things like detecting objects with magnets attached, like the lid of a box, or maybe a statue that unlocks your secret lair when placed on your mantle! The TLD493D excels at measuring nearby magnetic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
  Adafruit QT Py RP2040: Description What a cutie pie! Or is it... a QT Py? This diminutive dev board comes with one of our new favorite chip, the RP2040. It's been made famous in the new Raspberry Pi Pico and our Feather RP2040 and ItsyBitsy RP2040, but what if we wanted something really smol? A new chip means a new QT Py, and the Raspberry Pi RP2040 is no exception. When we saw this chip we thought "this chip is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
  LED Sequin - Emerald Green: Sew a little sparkle into your wearable project with an Adafruit LED Sequin. Simply connect 3 to 6VDC to the + pin and ground to the - pin, and the LED on the board will light up. You can make the LEDs fade and twinkle by using PWM.

// code stored in the sketch: diy-spacemouse.ino
#include <TinyUSB_Mouse_and_Keyboard.h>
#include <OneButton.h>
#include <Tlv493d.h>
#include <SimpleKalmanFilter.h>

Tlv493d mag = Tlv493d();
SimpleKalmanFilter xFilter(1, 1, 0.2), yFilter(1, 1, 0.2), zFilter(1, 1, 0.2);

// Setup buttons
OneButton button1(27, true);
OneButton button2(24, true);

float xOffset = 0, yOffset = 0, zOffset = 0;
float xCurrent = 0, yCurrent = 0, zCurrent = 0;

int calSamples = 300;
int sensivity = 8;
int magRange = 3;
int outRange = 127;      // Max allowed in HID report
float xyThreshold = 0.4; // Center threshold

int inRange = magRange * sensivity;
float zThreshold = xyThreshold * 1.5;

bool isOrbit = false;

void setup()
{

  button1.attachClick(goHome);
  button1.attachLongPressStop(goHome);

  button2.attachClick(fitToScreen);
  button2.attachLongPressStop(fitToScreen);

  // mouse and keyboard init
  Mouse.begin();
  Keyboard.begin();

  Serial.begin(9600);
  Wire1.begin();

  // mag sensor init
  mag.begin(Wire1);
  mag.setAccessMode(mag.MASTERCONTROLLEDMODE);
  mag.disableTemp();

  // crude offset calibration on first boot
  for (int i = 1; i <= calSamples; i++)
  {

    delay(mag.getMeasurementDelay());
    mag.updateData();

    xOffset += mag.getX();
    yOffset += mag.getY();
    zOffset += mag.getZ();

    Serial.print(".");
  }

  xOffset = xOffset / calSamples;
  yOffset = yOffset / calSamples;
  zOffset = zOffset / calSamples;

  Serial.println();
  Serial.println(xOffset);
  Serial.println(yOffset);
  Serial.println(zOffset);
}

void loop()
{

  // keep watching the push buttons
  button1.tick();
  button2.tick();

  // get the mag data
  delay(mag.getMeasurementDelay());
  mag.updateData();

  // update the filters
  xCurrent = xFilter.updateEstimate(mag.getX() - xOffset);
  yCurrent = yFilter.updateEstimate(mag.getY() - yOffset);
  zCurrent = zFilter.updateEstimate(mag.getZ() - zOffset);

  // check the center threshold
  if (abs(xCurrent) > xyThreshold || abs(yCurrent) > xyThreshold)
  {

    int xMove = 0;
    int yMove = 0;

    // map the magnetometer xy to the allowed 127 range in HID repports
    xMove = map(xCurrent, -inRange, inRange, -outRange, outRange);
    yMove = map(yCurrent, -inRange, inRange, -outRange, outRange);

    // press shift to orbit in Fusion 360 if the pan threshold is not corssed (zAxis)
    if (abs(zCurrent) < zThreshold && !isOrbit)
    {
      Keyboard.press(KEY_LEFT_SHIFT);
      isOrbit = true;
    }

    // pan or orbit by holding the middle mouse button and moving propotionaly to the xy axis
    Mouse.press(MOUSE_MIDDLE);
    Mouse.move(yMove, xMove, 0);
  }
  else
  {

    // release the mouse and keyboard if within the center threshold
    Mouse.release(MOUSE_MIDDLE);
    Keyboard.releaseAll();
    isOrbit = false;
  }

  Serial.print(xCurrent);
  Serial.print(",");
  Serial.print(yCurrent);
  Serial.print(",");
  Serial.print(zCurrent);
  Serial.println();
}

// go to home view in Fusion 360 by pressing  (CMD + SHIFT + H) shortcut assigned to the custom Add-in command
void goHome()
{
  Keyboard.press(KEY_LEFT_GUI);
  Keyboard.press(KEY_LEFT_SHIFT);
  Keyboard.write('h');

  delay(10);
  Keyboard.releaseAll();
  Serial.println("pressed home");
}

// fit to view by pressing the middle mouse button twice
void fitToScreen()
{
  Mouse.press(MOUSE_MIDDLE);
  Mouse.release(MOUSE_MIDDLE);
  Mouse.press(MOUSE_MIDDLE);
  Mouse.release(MOUSE_MIDDLE);

  Serial.println("pressed fit");
}
